# Fritzing sketch board-design (saved by Fritzing 1.0.3b)
breadboards: 1

parts:
  A1 = Esp32-c3 super mini
  Part1 = FC-28 Soil Hygrometer Module
  Part2 = FC-28 Soil Hygrometer Module - Probe
  PV1 = Generic Small 6V Solar Panel
  MOD1 = Multi booster
  Part3 = MCP73871 [part_number=MCP package=VQFN]
  U1 = LIPO-2000mAh [package=lipo-2000]
  Grove1 = Grove OLED 128x96

nets:
  N1: A1.Pin_4, Grove1.SDA
  N2: A1.Pin_5, Grove1.SCL
  N3: A1.Pin_12, Part1.AO
  VCC: A1.Pin_14, Part1.VCC, MOD1.V+, Grove1.VCC
  GND: A1.Pin_15, Part1.GND, PV1.-, MOD1.BAT-, MOD1.GND, Part3.Vss, U1.-, Grove1.GND
  N4: Part1.POS, Part2.POS
  N5: Part1.NEG, Part2.NEG
  N6: PV1.+, Part3.IN
  N7: MOD1.BAT+, Part3.OUT
  N8: Part3.VBAT, U1.+

custom parts:
  Esp32-c3 super mini: ESP32-C3 Development Board ESP32 SuperMini Development Board ESP32 Development Board WiFi Bluetooth.
  FC-28 Soil Hygrometer Module: The FC-28 is a soil hygrometer module that uses the Texas Instruments LM393 comparator chip to provide an analog measurement of soil humidity. The digital output is high when soil moisture is over a certain threshold, as determined by adjusting the potentiometer.
  FC-28 Soil Hygrometer Module - Probe: The FC-28 is a soil hygrometer module that uses the Texas Instruments LM393 comparator chip to provide an analog measurement of soil humidity.
  Multi booster: Input voltage range: 2.5V + Current: 1A Boost output voltage: 5V/ 8V/ 9V 12V ------------ A B VOUT ------------ 0 0 5V 0 1 8V 1 0 9V 1 1 12V ------------
  MCP73871: The MCP73871 device is a fully integrated linear solution for system load sharing and Li-Ion/Li-Polymer battery charge management with AC-DC wall adapter and USB port power sources selection. It is also capable of autonomous power source selection between input and battery. Along with its small physical size, the low number of required external components makes the device ideally suited for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
